# Fritzing sketch hw (saved by Fritzing 1.0.4)

parts:
  Part2 = Arduino Pro Mini v13
  R1 = Slide Potentiometer [maximum_resistance=10kΩ knob_status=50% power=0.5W package=THT]
  S2 = Taiway 100-SP-X-T1 SPDT Miniature Toggle Switch [part_number="2 position" package=THT]
  S5 = Momentary Switch [package=ksa_sealed_tac_switch]
  S6 = Momentary Switch [package=ksa_sealed_tac_switch]
  S7 = Momentary Switch [package=ksa_sealed_tac_switch]
  S8 = Momentary Switch [package=ksa_sealed_tac_switch]
  S9 = Taiway 100-SP-X-T1 SPDT Miniature Toggle Switch [part_number="2 position" package=THT]
  S10 = Taiway 100-SP-X-T1 SPDT Miniature Toggle Switch [part_number="2 position" package=THT]
  S11 = Taiway 100-SP-X-T1 SPDT Miniature Toggle Switch [part_number="2 position" package=THT]
  S12 = Taiway 100-SP-X-T1 SPDT Miniature Toggle Switch [part_number="2 position" package=THT]
  S13 = Round Pushbutton
  R2 = Rotary Potentiometer (Small) [maximum_resistance=10kΩ knob_status=50% power=0.5W package=THT]
  R3 = Rotary Potentiometer (Small) [maximum_resistance=10kΩ knob_status=50% power=0.5W package=THT]
  S14 = Taiway 100-SP-X-T1 SPDT Miniature Toggle Switch [part_number="3 position" package=THT]
  S15 = Taiway 100-SP-X-T1 SPDT Miniature Toggle Switch [part_number="3 position" package=THT]
  S16 = Taiway 100-SP-X-T1 SPDT Miniature Toggle Switch [part_number="3 position" package=THT]

nets:
  N1: Part2.GND, R1.leg2, R2.leg2, R3.leg2
  N2: Part2.A2, R1.wiper, R1.wiper-1, R2.wiper, R3.wiper
  N3: Part2.A1, S13.leg1, S14.L2
  N4: Part2.A0, S12.L1, S14.L1
  N5: Part2.D13/SCK, S5.3, S9.L1, S15.L2
  N6: Part2.D12/MISO, S6.3, S10.L1, S15.L1
  N7: Part2.D11_PWM/MOSI, S2.L1, S8.3, S16.L2
  N8: Part2.D10_PWM/SS, S7.3, S11.L1, S16.L1
  N9: Part2.D9_PWM, S14.COM, S15.COM, S16.COM
  N10: Part2.D8, S2.COM, S9.COM, S10.COM, S11.COM, S12.COM, R2.leg1
  N11: Part2.D2, S5.2, S7.2, S13.leg0
  N12: R1.leg1, S6.4, S7.4, S8.4
